# Fritzing sketch Small_colbs (saved by Fritzing 0.9.3b)

parts:
  Часть2 = Arduino Prototyping Shield
  Q1 = NPN-Transistor [package="TO92 [THT]"]
  Q2 = NPN-Transistor [package="TO92 [THT]"]
  Q3 = NPN-Transistor [package="TO92 [THT]"]
  Q4 = NPN-Transistor [package="TO92 [THT]"]
  Q5 = NPN-Transistor [package="TO92 [THT]"]
  Q6 = NPN-Transistor [package="TO92 [THT]"]
  Q7 = NPN-Transistor [package="TO92 [THT]"]
  LED1 = LED - 5mm [color="Red (633nm)" package="5 mm [THT]"]
  R1 = Resistor [tolerance=±5% resistance=220 package=THT]
  LED2 = LED - 5mm [color="Red (633nm)" package="5 mm [THT]"]
  LED3 = LED - 5mm [color="Red (633nm)" package="5 mm [THT]"]
  LED4 = LED - 5mm [color="Red (633nm)" package="5 mm [THT]"]
  LED5 = LED - 5mm [color="Red (633nm)" package="5 mm [THT]"]
  LED6 = LED - 5mm [color="Red (633nm)" package="5 mm [THT]"]
  LED7 = LED - 5mm [color="Red (633nm)" package="5 mm [THT]"]
  LED8 = RGB LED (com. cathode, rgb) [package="5 mm [THT]"]  # not connected
  L1 = Solenoid [part_number="Door lock"]
  Door_relay = OMRON PCB Power Relay – G5LE [part_number="G5LE-1\n" package=THT]
  +7V = Power plug
  +12V = Power plug
  S1 = Round Pushbutton
  S3 = Round Pushbutton
  S2 = Round Pushbutton
  S4 = Round Pushbutton
  RFM12b1 = RFM12b HopeRF Transceiver
  RFM12b2 = RFM12b HopeRF Transceiver
  RFM12b3 = RFM12b HopeRF Transceiver
  RFM12b4 = RFM12b HopeRF Transceiver
  LED9 = RGB LED (com. cathode, rgb) [package="5 mm [THT]"]  # not connected
  LED10 = RGB LED (com. cathode, rgb) [package="5 mm [THT]"]  # not connected
  LED11 = RGB LED (com. cathode, rgb) [package="5 mm [THT]"]  # not connected
  START = Round Pushbutton

nets:
  N1: Часть2.A0, S1.leg1
  N2: Часть2.A1, S2.leg1
  N3: Часть2.A2, S3.leg1
  N4: Часть2.A3, S4.leg1
  N5: Часть2.A4, START.leg1
  N6: Часть2.+5V, LED1.anode, LED2.anode, LED6.anode
  GND: Часть2.GND, Часть2.N$52, Часть2.N$107, Часть2.N$261, Часть2.N$263, Часть2.N$272, Часть2.N$297, Часть2.N$319, Q1.C, Q2.C, Q3.C, Q4.C, Q5.C, Q6.C, Q7.C, Door_relay.COIL1, +7V.GND, RFM12b4.8_ANT
  +9V: Часть2.+9V, +7V.VCC
  N7: Часть2.D8, Часть2.N$239, Q6.B
  N8: Часть2.D9, Часть2.N$143, Q5.B
  N9: Часть2.D13, R1.Pin_1
  N10: Часть2.D3, Часть2.N$380, Q4.B
  N11: Часть2.D4, Часть2.N$317, Q3.B
  N12: Часть2.D5, Часть2.N$281, Q2.B
  N13: Часть2.D6, Часть2.N$94, Q1.B
  N14: Часть2.D7, Часть2.N$305, Q7.B
  N15: Часть2.N$93, Часть2.N$321, Q4.E, LED2.cathode
  N16: Часть2.N$135, Q5.E
  N17: Часть2.N$178, Часть2.N$190, LED1.cathode, R1.Pin_0
  N18: Часть2.N$236, Q6.E, LED7.cathode
  N19: Часть2.N$269, Q7.E, LED6.cathode
  N20: Часть2.N$273, Q1.E, LED5.cathode
  N21: Часть2.N$282, Q2.E, LED4.cathode
  N22: Часть2.N$318, Q3.E, LED3.cathode
  N23: L1.pin1, +12V.VCC, RFM12b1.10_GND
  N24: Door_relay.B, +12V.GND, RFM12b1.9_VDD, RFM12b2.9_VDD, RFM12b3.9_VDD, RFM12b4.9_VDD
  N25: S1.leg0, S3.leg0, S2.leg0, S4.leg0, START.leg0
